# Fritzing sketch Motorized Fader Control (saved by Fritzing 0.7.1b)
breadboards: 1

parts:
  Arduino1 = Arduino
  VCC1 = Battery block 9V
  IC1 = H-Bridge [package=THT]
  R1 = Slide Potentiometer [maximum_resistance=100kΩ]
  M1 = DC Motor
  C1 = Electrolytic Capacitor [capacitance=1µF package="100 mil [THT, electrolytic]"]
  R2 = Resistor [tolerance=±5% resistance=1M package=THT]
  U1 = mystery part, 1 pin [chip_label="Touch Line" spacing=300mil]

nets:
  N1: Arduino1.D8, R2.Pin_0, U1.pin1
  N2: Arduino1.D7, R2.Pin_1
  N3: Arduino1.D5, IC1.2A
  N4: Arduino1.D3, IC1.1A
  N5: Arduino1.+5V, IC1.1_2EN, IC1.VCC1, R1.leg1
  GND: Arduino1.GND, VCC1.-, IC1.GND1, IC1.GND2, IC1.GND3, IC1.GND4, R1.leg2, C1.-
  N6: Arduino1.A0, R1.wiper
  N7: VCC1.+, IC1.VCC2, C1.+
  N8: IC1.1Y, M1.pin_1
  N9: IC1.2Y, M1.pin_2

notes:
  Motorized Fader Control, Arduino Motorized Fader Control by Cody Hazelwood, 1
  Fader Touch Line
